# Fritzing sketch Scheme (saved by Fritzing 0.9.4)
breadboards: 1

parts:
  Компонент1 = ESP-WROOM-32 [ESP-32S] Module [part_number=ESP-WROOM-32]
  LED1 = LED - 5mm [color="Red (633nm)" package="5 mm [THT]"]
  S1 = Pushbutton [package="[THT]"]
  R1 = Resistor [tolerance=±5% resistance=220 package=THT]

nets:
  N1: Компонент1.GND#0, S1.Pin_1, S1.Pin_2
  N2: Компонент1.IO34, LED1.anode
  N3: Компонент1.GND#51, R1.Pin_0
  N4: Компонент1.IO2, S1.Pin_3, S1.Pin_4
  N5: LED1.cathode, R1.Pin_1

custom parts:
  ESP-WROOM-32 [ESP-32S] Module: Espressif ESP-WROOM-32 WiFi/Bluetooth LE microcontroller module also known as the Ai-Thinker ESP-32S module with similar formfactor. The ESP32 is a microcontroller chip with WiFi and BLE capabilities. The chip is developed by Espressif and is the successor to the popular ESP8266 WiFi module.
